# Fritzing sketch HCDE_539_E2b (saved by Fritzing 0.9.3b)
breadboards: 1

parts:
  Part1 = Arduino Uno (Rev3)
  S1 = Pushbutton [package="[SMD]"]
  J1 = Piezo Speaker
  R1 = Resistor [tolerance=±5% resistance=10k package=THT]

nets:
  N1: Part1.D8, J1.pin2
  N2: Part1.D4, Part1.5V, S1.Pin_3, S1.Pin_4
  N3: Part1.GND, R1.Pin_1
